// Logisim project HERA.circ as structural Verilog: 9 circuits, main circuit main
module main (
);

  wire clk;
  wire [3:0] a, address, b, d;
  wire [4:0] F, Flags_out;
  wire [15:0] R_1, R_2, R_3, R_a, R_b, R_d;
  wire [15:12] instruction;

  Clock u_clk (.out(clk));
  ROM #(.addrWidth(4), .dataWidth(16)) rom_1 (.addr(address), .data({instruction, d, a, b}));
  PC pc_1 (.clk(clk), .addresss(address));
  RegisterBank registerbank_1 (
    .R_d(R_d), .d(d), .a(a), .b(b), .clk(clk), .R_1(R_1), .R_2(R_2), .R_3(R_3), .R_b(R_b), .R_a(R_a));
  FlagBank flagbank_1 (.clk(clk), .flags(F), .flags_out(Flags_out));
  DotMatrix #(.dotshape("circle"), .matrixrows(1)) dotmatrix_1 (
    .col0(F[0]), .col1(F[1]), .col2(F[2]), .col3(F[3]), .col4(F[4]));
  ALSU alsu_1 (
    .Flags(Flags_out), .R_a(R_a), .R_b(R_b), .Rd(R_d), .opcode(instruction), .d(d), .a(a), .b(b), .R_d(R_d),
    .Flags_out(F));
  Hex_Digit_Display hex_digit_display_1 (.value(address));  // open: dp
  Hex_Digit_Display hex_digit_display_2 (.value(instruction));  // open: dp
  Hex_Digit_Display hex_digit_display_3 (.value(R_1[15:12]));  // open: dp
  Hex_Digit_Display hex_digit_display_4 (.value(R_2[15:12]));  // open: dp
  Hex_Digit_Display hex_digit_display_5 (.value(R_3[15:12]));  // open: dp
  Hex_Digit_Display hex_digit_display_6 ();  // open: value, dp
  Hex_Digit_Display hex_digit_display_7 (.value(d));  // open: dp
  Hex_Digit_Display hex_digit_display_8 (.value(R_1[11:8]));  // open: dp
  Hex_Digit_Display hex_digit_display_9 (.value(R_2[11:8]));  // open: dp
  Hex_Digit_Display hex_digit_display_10 (.value(R_3[11:8]));  // open: dp
  Hex_Digit_Display hex_digit_display_11 ();  // open: value, dp
  Hex_Digit_Display hex_digit_display_12 ();  // open: value, dp
  Hex_Digit_Display hex_digit_display_13 (.value(a));  // open: dp
  Hex_Digit_Display hex_digit_display_14 (.value(b));  // open: dp
  Hex_Digit_Display hex_digit_display_15 (.value(R_1[7:4]));  // open: dp
  Hex_Digit_Display hex_digit_display_16 (.value(R_1[3:0]));  // open: dp
  Hex_Digit_Display hex_digit_display_17 (.value(R_2[7:4]));  // open: dp
  Hex_Digit_Display hex_digit_display_18 (.value(R_2[3:0]));  // open: dp
  Hex_Digit_Display hex_digit_display_19 (.value(R_3[7:4]));  // open: dp
  Hex_Digit_Display hex_digit_display_20 (.value(R_3[3:0]));  // open: dp

  // Other names for the same wires on the sheet: instruction[11:0] = {d, a, b}; opcode[3:0] = instruction

  // Notes on the sheet:
  //   contents of rom_1 (hex, n*v repeats v):
  //   e120 f14e e220 f24e a312
  //   Register Bank
  //   Main Module for HERA Processor
  //   Flag Bank
  //   Flags
  //   Flags: Sign, Zero, Overflow, Carry, CarryBlock
  //   Address
  //   Instructions
  //   Register 1
  //   Register 2
  //   Register 3
endmodule

// RegBank
module RegisterBank (
  input  [15:0] R_d,
  input  [3:0] d,
  input  [3:0] a,
  input  [3:0] b,
  input  clk,
  output [15:0] R_1,
  output [15:0] R_2,
  output [15:0] R_3,
  output [15:0] R_b,
  output [15:0] R_a
);

  wire R0_in, R1_in, R2_in, R3_in, R4_in, R5_in, R6_in, R7_in, R8_in, R9_in, R10_in, R11_in, R12_in, R13_in,
       R14_in, R15_in;
  wire [15:0] R0_out, R4_out, R5_out, R6_out, R7_out, R8_out, R9_out, R10_out, R11_out, R12_out, R13_out,
       R14_out, R15_out;

  Decoder #(.select(4)) decoder_1 (
    .out0(R0_in), .out1(R1_in), .out2(R2_in), .out3(R3_in), .out4(R4_in), .out5(R5_in), .out6(R6_in),
    .out7(R7_in), .out8(R8_in), .out9(R9_in), .out10(R10_in), .out11(R11_in), .out12(R12_in), .out13(R13_in),
    .out14(R14_in), .out15(R15_in), .sel(d));  // open: en
  Register #(.width(16)) R0 (.D({16{1'b0}}), .en(R0_in), .clk(clk), .Q(R0_out));  // open: clr
  Register #(.width(16)) R4 (.D(R_d), .en(R4_in), .clk(clk), .Q(R4_out));  // open: clr
  Register #(.width(16)) R8 (.D(R_d), .en(R8_in), .clk(clk), .Q(R8_out));  // open: clr
  Register #(.width(16)) R12 (.D(R_d), .en(R12_in), .clk(clk), .Q(R12_out));  // open: clr
  Register #(.width(16)) R1 (.D(R_d), .en(R1_in), .clk(clk), .Q(R_1));  // open: clr
  Register #(.width(16)) R5 (.D(R_d), .en(R6_in), .clk(clk), .Q(R5_out));  // open: clr
  Register #(.width(16)) R9 (.D(R_d), .en(R9_in), .clk(clk), .Q(R9_out));  // open: clr
  Register #(.width(16)) R13 (.D(R_d), .en(R13_in), .clk(clk), .Q(R13_out));  // open: clr
  Register #(.width(16)) R2 (.D(R_d), .en(R2_in), .clk(clk), .Q(R_2));  // open: clr
  Register #(.width(16)) R6 (.D(R_d), .en(R7_in), .clk(clk), .Q(R6_out));  // open: clr
  Register #(.width(16)) R10 (.D(R_d), .en(R10_in), .clk(clk), .Q(R10_out));  // open: clr
  Register #(.width(16)) R14 (.D(R_d), .en(R14_in), .clk(clk), .Q(R14_out));  // open: clr
  Register #(.width(16)) R3 (.D(R_d), .en(R3_in), .clk(clk), .Q(R_3));  // open: clr
  Register #(.width(16)) R7 (.D(R_d), .en(R7_in), .clk(clk), .Q(R7_out));  // open: clr
  Register #(.width(16)) R11 (.D(R_d), .en(R11_in), .clk(clk), .Q(R11_out));  // open: clr
  Register #(.width(16)) R15 (.D(R_d), .en(R15_in), .clk(clk), .Q(R15_out));  // open: clr
  Multiplexer #(.select(4), .width(16)) multiplexer_1 (
    .in0(R0_out), .in1(R_1), .in2(R_2), .in3(R_3), .in4(R4_out), .in5(R5_out), .in6(R6_out), .in7(R7_out),
    .in8(R8_out), .in9(R9_out), .in10(R10_out), .in11(R11_out), .in12(R12_out), .in13(R13_out),
    .in14(R14_out), .in15(R15_out), .out(R_a), .sel(a));
  Multiplexer #(.select(4), .width(16)) multiplexer_2 (
    .in0(R0_out), .in1(R_1), .in2(R_2), .in3(R_3), .in4(R4_out), .in5(R5_out), .in6(R6_out), .in7(R7_out),
    .in8(R8_out), .in9(R9_out), .in10(R10_out), .in11(R11_out), .in12(R12_out), .in13(R13_out),
    .in14(R14_out), .in15(R15_out), .out(R_b), .sel(b));

  // Other names for the same wires on the sheet: R1_out[15:0] = R_1; R2_out[15:0] = R_2; R3_out[15:0] = R_3

  // Notes on the sheet:
  //   Register Bank
  //   Register bank containing 16 16-bit registers
  //   We can read two registers R_a and R_b and write to R_d
endmodule

module ALSU (
  input  [4:0] Flags,
  input  [15:0] R_a,
  input  [15:0] R_b,
  input  [15:0] Rd,
  input  [3:0] opcode,
  input  [3:0] d,
  input  [3:0] a,
  input  [3:0] b,
  output [15:0] R_d,
  output [4:0] Flags_out
);

  wire and_1_out, comparator_1_eq, comparator_2_eq, comparator_3_eq;
  wire [4:0] F_arith, F_bitwise, flag_set_1_flags_out, ls_1_flags_out, multiplexer_2_out, multiplexer_3_out,
       or_1_out;
  wire [15:0] arith, bw, setlo, Shift;

  assign setlo = {{8{a[3]}}, {a, b}};  // Bit_Extender bit_extender_1
  Bitwise bitwise_1 (.R_a(R_a), .R_b(R_b), .op(opcode[2:0]), .Flags_in(Flags), .R_d(bw), .Flags_out(F_bitwise));
  Arithmetic arithmetic_1 (.R_a(R_a), .R_b(R_b), .op(opcode[2:0]), .Flags_in(Flags), .R_d(arith), .Flags_out(F_arith));
  LS ls_1 (.R_b_in(R_b), .op(a[2:0]), .Flags_in(Flags), .R_b_out(Shift), .Flags_out(ls_1_flags_out));
  Flag_Set flag_set_1 (
    .opcode(d[3:1]), .Fin_instruction({d[0], b}), .Flags_in(Flags), .Flags_out(flag_set_1_flags_out));  // open: out_5
  Multiplexer #(.select(4), .width(16)) multiplexer_1 (
    .in0({16{1'b0}}), .in1({16{1'b0}}), .in2({16{1'b0}}), .in3(Shift), .in4({16{1'b0}}), .in5({16{1'b0}}),
    .in6({16{1'b0}}), .in7({16{1'b0}}), .in8(bw), .in9(bw), .in10(arith), .in11(arith), .in12(arith),
    .in13(bw), .in14(setlo), .in15({a, b, Rd[7:0]}), .out(R_d), .sel(opcode));
  Comparator #(.width(4)) comparator_1 (.a(a), .b(4'b0110), .eq(comparator_1_eq));  // open: gt, lt
  Comparator #(.width(4)) comparator_2 (.a(opcode), .b(4'b0011), .eq(comparator_2_eq));  // open: gt, lt
  Comparator #(.width(4)) comparator_3 (.a(opcode), .b(4'b0011), .eq(comparator_3_eq));  // open: gt, lt
  Multiplexer #(.width(5)) multiplexer_2 (
    .in0(Flags), .in1(flag_set_1_flags_out), .out(multiplexer_2_out), .sel(and_1_out));
  and and_1 (and_1_out, comparator_2_eq, comparator_1_eq);
  Multiplexer #(.width(5)) multiplexer_3 (
    .in0(Flags), .in1(ls_1_flags_out), .out(multiplexer_3_out), .sel(comparator_3_eq));
  assign or_1_out = multiplexer_2_out | multiplexer_3_out;  // OR_Gate or_1, 5 bits wide
  Multiplexer #(.select(4), .width(5)) multiplexer_4 (
    .in0(Flags), .in1(Flags), .in2(Flags), .in3(or_1_out), .in4(Flags), .in5(Flags), .in6(Flags),
    .in7(Flags), .in8(F_bitwise), .in9(F_bitwise), .in10(F_arith), .in11(F_arith), .in12(F_arith),
    .in13(F_bitwise), .in14(Flags), .in15(Flags), .out(Flags_out), .sel(opcode));

  // Other names for the same wires on the sheet: sethi[15:0] = {a, b, Rd[7:0]}; F[4:0] = Flags

  // Notes on the sheet:
  //   ALSU
  //   SETLO logic
  //   Bitwise instructions (AND, OR, XOR)
  //   Arithmetic instructions (ADD, SUB, MUL)
  //   Module that handles arithmetic and other operations done on values stored in register bank
  //   11:8
  //   7:4
  //   3:0
  //   15:12
  //   Flag Instructions
  //   Flag opcode
  //   Input Flags
  //   Manually setting flags
  //   Shift Instructions
  //   Shift opcode
endmodule

module PC (
  input  clk,
  output [3:0] addresss
);

  Counter #(.max('hf), .width(4)) counter_1 (.clk(clk), .Q(addresss));  // open: clr, load, up, count, D, carry

  // Notes on the sheet:
  //   Program counter:  
  //   We read through four bit addresses that are fed into our ROM to retrieve instructions for the CPU. 
endmodule

// Flags
module FlagBank (
  input  clk,
  input  [4:0] flags,
  output [4:0] flags_out
);

  wire reset;

  D_Flip_Flop Sign (.D(flags[0]), .clk(clk), .Q(flags_out[0]), .reset(reset));  // open: Qn, preset
  D_Flip_Flop Carry (.D(flags[3]), .clk(clk), .Q(flags_out[3]), .reset(reset));  // open: Qn, preset
  D_Flip_Flop Zero (.D(flags[1]), .clk(clk), .Q(flags_out[1]), .reset(reset));  // open: Qn, preset
  D_Flip_Flop Carryblock (.D(flags[4]), .clk(clk), .Q(flags_out[4]), .reset(reset));  // open: Qn, preset
  D_Flip_Flop Overflow (.D(flags[2]), .clk(clk), .Q(flags_out[2]), .reset(reset));  // open: Qn, preset

  // Other names for the same wires on the sheet: F0 = flags[0]; F1 = flags[1]; F2 = flags[2]; F3 = flags[3];
  //   F4 = flags[4]; F0_out = flags_out[0]; F1_out = flags_out[1]; F2_out = flags_out[2]; F3_out = flags_out[3];
  //   F4_out = flags_out[4]

  // Notes on the sheet:
  //   Flag bank: consists of five D-flip flops to store the current state of each flag
endmodule

// F_Set
module Flag_Set (
  input  [2:0] opcode,
  input  [4:0] Fin_instruction,
  input  [4:0] Flags_in,
  output [4:0] Flags_out,
  output [4:0] out_5
);

  wire [4:0] FON;

  assign FON = Fin_instruction | Flags_in;  // OR_Gate or_1, 5 bits wide
  assign out_5 = Flags_in & ~Fin_instruction;  // AND_Gate and_1, 5 bits wide
  Multiplexer #(.select(3), .width(5)) multiplexer_1 (
    .in0(FON), .in1(Fin_instruction), .in2(Flags_in), .in3(Flags_in), .in4(out_5), .in5(Flags_in),
    .in6({Flags_in[4], Fin_instruction[3:0]}), .in7(Flags_in), .out(Flags_out), .sel(opcode));

  // Other names for the same wires on the sheet: FOFF[4:0] = out_5; FSET4[4:0] = {Flags_in[4], Fin_instruction[3:0]};
  //   FSET5[4:0] = Fin_instruction; cb_flag = Flags_in[4]

  // Notes on the sheet:
  //   Manually Setting Flags
  //   Given the instructions, we can manually turn on and off flags.
  //   FSET4 leaves carry block flag unchanged 
endmodule

module LS (
  input  [15:0] R_b_in,
  input  [2:0] op,
  input  [4:0] Flags_in,
  output [15:0] R_b_out,
  output [4:0] Flags_out
);

  wire and_1_out, and_2_out, decoder_1_out0, decoder_1_out1;
  wire [15:0] shifter_1_out, shifter_2_out;

  Decoder #(.select(3)) decoder_1 (
    .out0(decoder_1_out0), .out1(decoder_1_out1), .sel(op));  // open: out2, out3, out4, out5, out6, out7, en
  Shifter #(.width(16)) shifter_1 (.in(R_b_in), .\dist (4'b0001), .out(shifter_1_out));
  Shifter #(.shift("lr"), .width(16)) shifter_2 (.in(R_b_in), .\dist (4'b0001), .out(shifter_2_out));
  and and_1 (and_1_out, R_b_in[15], decoder_1_out0);
  and and_2 (and_2_out, R_b_in[0], decoder_1_out1);
  or or_1 (Flags_out[3], and_1_out, and_2_out);
  Multiplexer #(.select(3), .width(16)) multiplexer_1 (
    .in0(shifter_1_out), .in1(shifter_2_out), .in2({16{1'b0}}), .in3({16{1'b0}}), .in4({16{1'b0}}),
    .in5({16{1'b0}}), .in6({16{1'b0}}), .in7({16{1'b0}}), .out(R_b_out), .sel(op));

  assign {Flags_out[4], Flags_out[2:0]} = {Flags_in[4], Flags_in[2:0]};

  // Other names for the same wires on the sheet: low = R_b_in[0]; high = R_b_in[15]

  // Notes on the sheet:
  //   Logical Shift Operations
  //   Module for performing various logical shift operations on the value stored in a given register 
  //   Logical Shift Left
  //   Logical Shift Right
  //   check if bit is 1 on far left or right: if yes then depending on whether its a logical shift right or left then turn on carry flag 
endmodule

module Bitwise (
  input  [15:0] R_a,
  input  [15:0] R_b,
  input  [2:0] op,
  input  [4:0] Flags_in,
  output [15:0] R_d,
  output [4:0] Flags_out
);

  wire [15:0] AND, OR, XOR;

  assign AND = R_a & R_b;  // AND_Gate AND, 16 bits wide
  assign OR = R_a | R_b;  // OR_Gate OR, 16 bits wide
  assign XOR = R_a ^ R_b;  // XOR_Gate XOR, 16 bits wide
  Multiplexer #(.select(3), .width(16)) multiplexer_1 (
    .in0(AND), .in1(OR), .in5(XOR), .out({Flags_out[0], R_d[14:0]}), .sel(op));  // open: in2, in3, in4, in6, in7
  Comparator #(.width(16)) comparator_1 (
    .a({Flags_out[0], R_d[14:0]}), .b({16{1'b0}}), .eq(Flags_out[1]));  // open: gt, lt

  assign Flags_out[4:2] = Flags_in[4:2];
  assign R_d[15] = Flags_out[0];

  // Other names for the same wires on the sheet: z = Flags_out[1]; s = Flags_out[0]

  // Notes on the sheet:
  //   Bitwise instructions 
  //   AND logic
  //   OR logic
  //   XOR logic
  //   set s to B_15 of the result
endmodule

module Arithmetic (
  input  [15:0] R_a,
  input  [15:0] R_b,
  input  [2:0] op,
  input  [4:0] Flags_in,
  output [15:0] R_d,
  output [4:0] Flags_out
);

  wire adder_1_cout, c14, subtractor_1_bout;
  wire [1:0] c_add, c_sub;
  wire [15:0] ADD, MUL, SUB;

  Multiplier #(.width(16)) multiplier_1 (.a(R_a), .b(R_b), .out(MUL));  // open: cin, cout
  xor xor_1 (Flags_out[2], Flags_out[3], c14);
  Adder #(.width(14)) adder_1 (.a(R_a[13:0]), .b(R_b[13:0]), .out(ADD[13:0]), .cout(adder_1_cout));  // open: cin
  Subtractor #(.width(14)) subtractor_1 (
    .a(R_a[13:0]), .b(R_b[13:0]), .out(SUB[13:0]), .bout(subtractor_1_bout));  // open: bin
  Adder #(.width(1)) adder_2 (.a(R_a[14]), .b(R_b[14]), .out(ADD[14]), .cin(adder_1_cout), .cout(c_add[0]));
  Subtractor #(.width(1)) subtractor_2 (
    .a(R_a[14]), .b(R_b[14]), .out(SUB[14]), .bin(subtractor_1_bout), .bout(c_sub[0]));
  Adder #(.width(1)) adder_3 (.a(R_a[15]), .b(R_b[15]), .out(ADD[15]), .cin(c_add[0]), .cout(c_add[1]));
  Subtractor #(.width(1)) subtractor_3 (.a(R_a[15]), .b(R_b[15]), .out(SUB[15]), .bin(c_sub[0]), .bout(c_sub[1]));
  Multiplexer #(.select(3), .width(16)) multiplexer_1 (
    .in0({16{1'b0}}), .in1({16{1'b0}}), .in2(ADD), .in3(SUB), .in4(MUL), .in5({16{1'b0}}), .in6({16{1'b0}}),
    .in7({16{1'b0}}), .out(R_d), .sel(op));
  Multiplexer #(.select(3), .width(2)) multiplexer_2 (
    .in0(2'b00), .in1(2'b00), .in2(c_add), .in3(c_sub), .in4(2'b00), .in5(2'b00), .in6(2'b00), .in7(2'b00),
    .out({Flags_out[3], c14}), .sel(op));

  assign {Flags_out[4], Flags_out[1:0]} = {Flags_in[4], Flags_in[1:0]};

  // Other names for the same wires on the sheet: c15 = Flags_out[3]; ADD_013[13:0] = ADD[13:0]; ADD_14 = ADD[14];
  //   ADD_15 = ADD[15]; SUB_013[13:0] = SUB[13:0]; SUB_14 = SUB[14]; SUB_15 = SUB[15]

  // Notes on the sheet:
  //   ADD logic
  //   SUB logic
  //   Arithmetic Instructions
  //   MUL logic
endmodule
